// Logisim project Proj_1_HF26.circ as structural Verilog: 6 circuits, main circuit main
module main (
);

  wire clock_1_out, dec_7seg_driver_1_out_5, dec_7seg_driver_1_out_6, dec_7seg_driver_1_out_7,
       dec_7seg_driver_1_out_8, dec_7seg_driver_1_out_9, dec_7seg_driver_1_out_10, dec_7seg_driver_1_out_11,
       dec_7seg_driver_2_out_5, dec_7seg_driver_2_out_6, dec_7seg_driver_2_out_7, dec_7seg_driver_2_out_8,
       dec_7seg_driver_2_out_9, dec_7seg_driver_2_out_10, dec_7seg_driver_2_out_11, dec_counter_1__0,
       dec_counter_1__1, dec_counter_1__2, dec_counter_1__3, dec_counter_1_is_nine, dec_counter_2__0,
       dec_counter_2__1, dec_counter_2__2, dec_counter_2__3;

  Clock clock_1 (.out(clock_1_out));
  dec_counter dec_counter_1 (
    .Clock(clock_1_out), .IS_NINE(dec_counter_1_is_nine), ._0(dec_counter_1__0), ._1(dec_counter_1__1),
    ._2(dec_counter_1__2), ._3(dec_counter_1__3));
  dec_counter dec_counter_2 (
    .Clock(dec_counter_1_is_nine), ._0(dec_counter_2__0), ._1(dec_counter_2__1), ._2(dec_counter_2__2),
    ._3(dec_counter_2__3));  // open: IS_NINE
  dec_7seg_driver dec_7seg_driver_1 (
    .in_1(dec_counter_1__0), .in_2(dec_counter_1__1), .in_3(dec_counter_1__2), .in_4(dec_counter_1__3),
    .out_5(dec_7seg_driver_1_out_5), .out_6(dec_7seg_driver_1_out_6), .out_7(dec_7seg_driver_1_out_7),
    .out_8(dec_7seg_driver_1_out_8), .out_9(dec_7seg_driver_1_out_9), .out_10(dec_7seg_driver_1_out_10),
    .out_11(dec_7seg_driver_1_out_11));
  dec_7seg_driver dec_7seg_driver_2 (
    .in_1(dec_counter_2__0), .in_2(dec_counter_2__1), .in_3(dec_counter_2__2), .in_4(dec_counter_2__3),
    .out_5(dec_7seg_driver_2_out_5), .out_6(dec_7seg_driver_2_out_6), .out_7(dec_7seg_driver_2_out_7),
    .out_8(dec_7seg_driver_2_out_8), .out_9(dec_7seg_driver_2_out_9), .out_10(dec_7seg_driver_2_out_10),
    .out_11(dec_7seg_driver_2_out_11));
  _7_Segment_Display u_7_segment_display_1 (
    .g(dec_7seg_driver_2_out_11), .f(dec_7seg_driver_2_out_10), .a(dec_7seg_driver_2_out_5),
    .b(dec_7seg_driver_2_out_6), .e(dec_7seg_driver_2_out_9), .d(dec_7seg_driver_2_out_8),
    .c(dec_7seg_driver_2_out_7));  // open: dp
  _7_Segment_Display u_7_segment_display_2 (
    .g(dec_7seg_driver_1_out_11), .f(dec_7seg_driver_1_out_10), .a(dec_7seg_driver_1_out_5),
    .b(dec_7seg_driver_1_out_6), .e(dec_7seg_driver_1_out_9), .d(dec_7seg_driver_1_out_8),
    .c(dec_7seg_driver_1_out_7));  // open: dp
endmodule

module bonus (
);

  wire clock_1_out, hex_7seg_driver_1_out_5, hex_7seg_driver_1_out_6, hex_7seg_driver_1_out_7,
       hex_7seg_driver_1_out_8, hex_7seg_driver_1_out_9, hex_7seg_driver_1_out_10, hex_7seg_driver_1_out_11,
       hex_7seg_driver_2_out_5, hex_7seg_driver_2_out_6, hex_7seg_driver_2_out_7, hex_7seg_driver_2_out_8,
       hex_7seg_driver_2_out_9, hex_7seg_driver_2_out_10, hex_7seg_driver_2_out_11, hex_counter_1__0,
       hex_counter_1__1, hex_counter_1__2, hex_counter_1__3, hex_counter_1_is_fifteen, hex_counter_2__0,
       hex_counter_2__1, hex_counter_2__2, hex_counter_2__3;

  Clock clock_1 (.out(clock_1_out));
  hex_counter hex_counter_1 (
    .Clock(clock_1_out), .IS_FIFTEEN(hex_counter_1_is_fifteen), ._0(hex_counter_1__0), ._1(hex_counter_1__1),
    ._2(hex_counter_1__2), ._3(hex_counter_1__3));
  hex_counter hex_counter_2 (
    .Clock(hex_counter_1_is_fifteen), ._0(hex_counter_2__0), ._1(hex_counter_2__1), ._2(hex_counter_2__2),
    ._3(hex_counter_2__3));  // open: IS_FIFTEEN
  hex_7seg_driver hex_7seg_driver_1 (
    .in_1(hex_counter_1__0), .in_2(hex_counter_1__1), .in_3(hex_counter_1__2), .in_4(hex_counter_1__3),
    .out_5(hex_7seg_driver_1_out_5), .out_6(hex_7seg_driver_1_out_6), .out_7(hex_7seg_driver_1_out_7),
    .out_8(hex_7seg_driver_1_out_8), .out_9(hex_7seg_driver_1_out_9), .out_10(hex_7seg_driver_1_out_10),
    .out_11(hex_7seg_driver_1_out_11));
  hex_7seg_driver hex_7seg_driver_2 (
    .in_1(hex_counter_2__0), .in_2(hex_counter_2__1), .in_3(hex_counter_2__2), .in_4(hex_counter_2__3),
    .out_5(hex_7seg_driver_2_out_5), .out_6(hex_7seg_driver_2_out_6), .out_7(hex_7seg_driver_2_out_7),
    .out_8(hex_7seg_driver_2_out_8), .out_9(hex_7seg_driver_2_out_9), .out_10(hex_7seg_driver_2_out_10),
    .out_11(hex_7seg_driver_2_out_11));
  _7_Segment_Display u_7_segment_display_1 (
    .g(hex_7seg_driver_2_out_11), .f(hex_7seg_driver_2_out_10), .a(hex_7seg_driver_2_out_5),
    .b(hex_7seg_driver_2_out_6), .e(hex_7seg_driver_2_out_9), .d(hex_7seg_driver_2_out_8),
    .c(hex_7seg_driver_2_out_7));  // open: dp
  _7_Segment_Display u_7_segment_display_2 (
    .g(hex_7seg_driver_1_out_11), .f(hex_7seg_driver_1_out_10), .a(hex_7seg_driver_1_out_5),
    .b(hex_7seg_driver_1_out_6), .e(hex_7seg_driver_1_out_9), .d(hex_7seg_driver_1_out_8),
    .c(hex_7seg_driver_1_out_7));  // open: dp
endmodule

module dec_7seg_driver (
  input  in_1,
  input  in_2,
  input  in_3,
  input  in_4,
  output out_5,
  output out_6,
  output out_7,
  output out_8,
  output out_9,
  output out_10,
  output out_11
);

  segment_a segment_a_1 (._0(in_1), ._1(in_2), ._2(in_3), ._3(in_4), .out_5(out_5));
  segment_b segment_b_1 (._0(in_1), ._1(in_2), ._2(in_3), ._3(in_4), .out_5(out_6));
  segment_c segment_c_1 (._0(in_1), ._1(in_2), ._2(in_3), ._3(in_4), .out_5(out_7));
  segment_d segment_d_1 (._0(in_1), ._1(in_2), ._2(in_3), ._3(in_4), .out_5(out_8));
  segment_e segment_e_1 (._0(in_1), ._1(in_2), ._2(in_3), ._3(in_4), .out_5(out_9));
  segment_f segment_f_1 (._0(in_1), ._1(in_2), ._2(in_3), ._3(in_4), .out_5(out_10));
  segment_g segment_g_1 (._0(in_1), ._1(in_2), ._2(in_3), ._3(in_4), .out_5(out_11));
endmodule

module dec_counter (
  input  Clock,
  output _0,
  output _1,
  output _2,
  output _3,
  output IS_NINE
);

  wire and_2_out, and_3_out, and_4_out, and_5_out, and_6_out, and_7_out, and_8_out, D1_qn, D2_qn, D3_qn,
       D4_qn, or_1_out, or_2_out, or_3_out;

  and and_1 (IS_NINE, _3, D2_qn, D3_qn, _0);
  and and_2 (and_2_out, _3, D4_qn);
  and and_3 (and_3_out, _2, _1, _0);
  and and_4 (and_4_out, _2, D3_qn);
  and and_5 (and_5_out, _2, D4_qn);
  and and_6 (and_6_out, D2_qn, _1, _0);
  and and_7 (and_7_out, _1, D4_qn);
  and and_8 (and_8_out, D1_qn, D3_qn, _0);
  or or_1 (or_1_out, and_2_out, and_3_out);
  or or_2 (or_2_out, and_4_out, and_5_out, and_6_out);
  or or_3 (or_3_out, and_7_out, and_8_out);
  D_Flip_Flop #(.trigger("falling")) D1 (.clk(Clock), .D(or_1_out), .Q(_3), .Qn(D1_qn));  // open: preset, en, reset
  D_Flip_Flop #(.trigger("falling")) D2 (.clk(Clock), .D(or_2_out), .Q(_2), .Qn(D2_qn));  // open: preset, en, reset
  D_Flip_Flop #(.trigger("falling")) D3 (.clk(Clock), .D(or_3_out), .Q(_1), .Qn(D3_qn));  // open: preset, en, reset
  D_Flip_Flop #(.trigger("falling")) D4 (.clk(Clock), .D(D4_qn), .Q(_0), .Qn(D4_qn));  // open: preset, en, reset
endmodule

module hex_7seg_driver (
  input  in_1,
  input  in_2,
  input  in_3,
  input  in_4,
  output out_5,
  output out_6,
  output out_7,
  output out_8,
  output out_9,
  output out_10,
  output out_11
);

  segment_a segment_a_1 (._0(in_1), ._1(in_2), ._2(in_3), ._3(in_4), .out_5(out_5));
  segment_b segment_b_1 (._0(in_1), ._1(in_2), ._2(in_3), ._3(in_4), .out_5(out_6));
  segment_c segment_c_1 (._0(in_1), ._1(in_2), ._2(in_3), ._3(in_4), .out_5(out_7));
  segment_d segment_d_1 (._0(in_1), ._1(in_2), ._2(in_3), ._3(in_4), .out_5(out_8));
  segment_e segment_e_1 (._0(in_1), ._1(in_2), ._2(in_3), ._3(in_4), .out_5(out_9));
  segment_f segment_f_1 (._0(in_1), ._1(in_2), ._2(in_3), ._3(in_4), .out_5(out_10));
  segment_g segment_g_1 (._0(in_1), ._1(in_2), ._2(in_3), ._3(in_4), .out_5(out_11));
endmodule

module hex_counter (
  input  Clock,
  output _0,
  output _1,
  output _2,
  output _3,
  output IS_FIFTEEN
);

  wire and_2_out, and_3_out, and_4_out, and_5_out, and_6_out, and_7_out, and_8_out, and_9_out, and_10_out,
       D1_qn, D2_qn, D3_qn, D4_qn, or_1_out, or_2_out, or_3_out;

  and and_1 (IS_FIFTEEN, _3, _2, _1, _0);
  and and_2 (and_2_out, _3, D2_qn);
  and and_3 (and_3_out, _3, D3_qn);
  and and_4 (and_4_out, _3, D4_qn);
  and and_5 (and_5_out, D1_qn, _2, _1, _0);
  and and_6 (and_6_out, _2, D3_qn);
  and and_7 (and_7_out, _2, D4_qn);
  and and_8 (and_8_out, D2_qn, _1, _0);
  and and_9 (and_9_out, _1, D4_qn);
  and and_10 (and_10_out, D3_qn, _0);
  or or_1 (or_1_out, and_2_out, and_3_out, and_4_out, and_5_out);
  or or_2 (or_2_out, and_6_out, and_7_out, and_8_out);
  or or_3 (or_3_out, and_9_out, and_10_out);
  D_Flip_Flop #(.trigger("falling")) D1 (.clk(Clock), .D(or_1_out), .Q(_3), .Qn(D1_qn));  // open: preset, en, reset
  D_Flip_Flop #(.trigger("falling")) D2 (.clk(Clock), .D(or_2_out), .Q(_2), .Qn(D2_qn));  // open: preset, en, reset
  D_Flip_Flop #(.trigger("falling")) D3 (.clk(Clock), .D(or_3_out), .Q(_1), .Qn(D3_qn));  // open: preset, en, reset
  D_Flip_Flop #(.trigger("falling")) D4 (.clk(Clock), .D(D4_qn), .Q(_0), .Qn(D4_qn));  // open: preset, en, reset
endmodule
