// Logisim project segment_abc_dec.circ as structural Verilog: 3 circuits, main circuit segment_a
module segment_a (
  input  _0,
  input  _1,
  input  _2,
  input  _3,
  output out_5
);

  wire not_1_out, not_2_out, not_3_out, not_4_out, or_1_out, xnor_1_out;

  not not_1 (not_1_out, _0);
  not not_2 (not_2_out, _1);
  not not_3 (not_3_out, _2);
  not not_4 (not_4_out, _3);
  xnor xnor_1 (xnor_1_out, _0, _2);
  or or_1 (or_1_out, _1, _3);
  or or_2 (out_5, xnor_1_out, or_1_out);
endmodule

module segment_b (
  input  _0,
  input  _1,
  input  _2,
  input  _3,
  output out_5
);

  wire not_1_out, not_2_out, not_3_out, not_4_out, or_1_out, xnor_1_out;

  not not_1 (not_1_out, _0);
  not not_2 (not_2_out, _1);
  not not_3 (not_3_out, _2);
  not not_4 (not_4_out, _3);
  xnor xnor_1 (xnor_1_out, _1, _0);
  or or_1 (or_1_out, _3, not_3_out);
  or or_2 (out_5, xnor_1_out, or_1_out);
endmodule

module segment_c (
  input  _0,
  input  _1,
  input  _2,
  input  _3,
  output out_5
);

  wire not_1_out, not_2_out, not_3_out, not_4_out, or_1_out;

  not not_1 (not_1_out, _0);
  not not_2 (not_2_out, _1);
  not not_3 (not_3_out, _2);
  not not_4 (not_4_out, _3);
  or or_1 (or_1_out, _0, not_2_out);
  or or_2 (out_5, or_1_out, _2);
endmodule
