// Logisim project segment_abc_hex.circ as structural Verilog: 3 circuits, main circuit segment_a
module segment_a (
  input  _0,
  input  _1,
  input  _2,
  input  _3,
  output out_5
);

  wire and_1_out, and_2_out, not_1_out, not_2_out, not_3_out, not_4_out, or_1_out, or_2_out, xor_1_out,
       xor_2_out;

  not not_1 (not_1_out, _0);
  not not_2 (not_2_out, _1);
  not not_3 (not_3_out, _2);
  not not_4 (not_4_out, _3);
  xor xor_1 (xor_1_out, _0, _3);
  xor xor_2 (xor_2_out, _3, _1);
  or or_1 (or_1_out, xor_1_out, _1);
  or or_2 (or_2_out, xor_2_out, not_1_out);
  and and_1 (and_1_out, _2, or_1_out);
  and and_2 (and_2_out, not_3_out, or_2_out);
  or or_3 (out_5, and_1_out, and_2_out);
endmodule

module segment_b (
  input  _0,
  input  _1,
  input  _2,
  input  _3,
  output out_5
);

  wire and_1_out, and_2_out, and_3_out, and_4_out, not_1_out, not_2_out, not_3_out, not_4_out, or_1_out,
       or_2_out, xor_1_out;

  not not_1 (not_1_out, _0);
  not not_2 (not_2_out, _1);
  not not_3 (not_3_out, _2);
  not not_4 (not_4_out, _3);
  xor xor_1 (xor_1_out, _1, _3);
  and and_1 (and_1_out, not_2_out, not_4_out);
  and and_2 (and_2_out, and_1_out, not_1_out);
  and and_3 (and_3_out, not_3_out, or_1_out);
  or or_1 (or_1_out, not_4_out, not_1_out);
  and and_4 (and_4_out, _0, xor_1_out);
  or or_2 (or_2_out, and_2_out, and_3_out);
  or or_3 (out_5, and_4_out, or_2_out);
endmodule

module segment_c (
  input  _0,
  input  _1,
  input  _2,
  input  _3,
  output out_5
);

  wire and_1_out, and_2_out, not_1_out, not_2_out, not_4_out, or_1_out, or_2_out, xor_1_out;

  not not_1 (not_1_out, _0);
  not not_2 (not_2_out, _1);
  // NOT_Gate not_3 has open pins: in=_2, out=open
  not not_4 (not_4_out, _3);
  and and_1 (and_1_out, not_2_out, not_4_out);
  and and_2 (and_2_out, _0, or_1_out);
  or or_1 (or_1_out, not_2_out, not_4_out);
  xor xor_1 (xor_1_out, _3, _2);
  or or_2 (or_2_out, and_1_out, and_2_out);
  or or_3 (out_5, xor_1_out, or_2_out);
endmodule
