// Logisim project segment_de_dec.circ as structural Verilog: 2 circuits, main circuit segment_d
module segment_d (
  input  _0,
  input  _1,
  input  _2,
  input  _3,
  output out_5
);

  wire and_1_out, and_2_out, not_1_out, not_2_out, not_3_out, not_4_out, or_1_out, or_2_out, xor_1_out;

  not not_1 (not_1_out, _0);
  not not_2 (not_2_out, _1);
  not not_3 (not_3_out, _2);
  not not_4 (not_4_out, _3);
  xor xor_1 (xor_1_out, _1, _2);
  and and_1 (and_1_out, xor_1_out, _0);
  or or_1 (or_1_out, not_3_out, _1);
  or or_2 (or_2_out, and_1_out, _3);
  and and_2 (and_2_out, not_1_out, or_1_out);
  or or_3 (out_5, or_2_out, and_2_out);
endmodule

module segment_e (
  input  _0,
  input  _1,
  input  _2,
  input  _3,
  output out_5
);

  wire not_1_out, not_2_out, not_3_out, not_4_out, or_1_out;

  not not_1 (not_1_out, _0);
  not not_2 (not_2_out, _1);
  not not_3 (not_3_out, _2);
  not not_4 (not_4_out, _3);
  or or_1 (or_1_out, _1, not_3_out);
  and and_1 (out_5, not_1_out, or_1_out);
endmodule
