// Logisim project segment_fg_hex.circ as structural Verilog: 2 circuits, main circuit segment_f
module segment_f (
  input  _0,
  input  _1,
  input  _2,
  input  _3,
  output out_5
);

  wire and_1_out, and_2_out, not_1_out, not_2_out, not_3_out, not_4_out, or_1_out, xor_1_out;

  not not_1 (not_1_out, _0);
  not not_2 (not_2_out, _1);
  not not_3 (not_3_out, _2);
  not not_4 (not_4_out, _3);
  xor xor_1 (xor_1_out, _2, _3);
  and and_1 (and_1_out, not_1_out, not_2_out);
  or or_1 (or_1_out, xor_1_out, and_1_out);
  and and_2 (and_2_out, _2, _1);
  or or_2 (out_5, or_1_out, and_2_out);
endmodule

module segment_g (
  input  _0,
  input  _1,
  input  _2,
  input  _3,
  output out_5
);

  wire and_1_out, and_2_out, and_3_out, and_4_out, not_1_out, not_2_out, not_3_out, not_4_out, or_1_out,
       or_2_out, xor_1_out;

  not not_1 (not_1_out, _0);
  not not_2 (not_2_out, _1);
  not not_3 (not_3_out, _2);
  not not_4 (not_4_out, _3);
  and and_1 (and_1_out, not_1_out, _1);
  and and_2 (and_2_out, _0, _3);
  and and_3 (and_3_out, not_3_out, _3);
  and and_4 (and_4_out, not_4_out, xor_1_out);
  xor xor_1 (xor_1_out, _2, _1);
  or or_1 (or_1_out, and_1_out, and_2_out);
  or or_2 (or_2_out, and_3_out, and_4_out);
  or or_3 (out_5, or_1_out, or_2_out);
endmodule
